// Logisim project updown.circ as structural Verilog: 1 circuit, main circuit main
module main (
);

  wire and_1_out, clock_1_out, clock_2_out, d_ff_1_q, d_ff_1_qn, d_ff_2_q, d_ff_2_qn, d_ff_3_q, d_ff_3_qn,
       not_1_out, Q0, Q1, Q2, Reset, stop, Up_Down;

  Clock clock_1 (.out(clock_1_out));
  xor xor_1 (Q0, Up_Down, d_ff_1_q);
  D_Flip_Flop d_ff_1 (
    .clk(clock_1_out), .D(d_ff_1_qn), .Q(d_ff_1_q), .Qn(d_ff_1_qn), .preset(Reset));  // open: en, reset
  xor xor_2 (Q1, Up_Down, d_ff_2_q);
  D_Flip_Flop d_ff_2 (.clk(d_ff_1_qn), .D(d_ff_2_qn), .Q(d_ff_2_q), .Qn(d_ff_2_qn), .preset(Reset));  // open: en, reset
  xor xor_3 (Q2, Up_Down, d_ff_3_q);
  D_Flip_Flop d_ff_3 (.clk(d_ff_2_qn), .D(d_ff_3_qn), .Q(d_ff_3_q), .Qn(d_ff_3_qn), .preset(Reset));  // open: en, reset
  Clock clock_2 (.out(clock_2_out));
  not not_1 (not_1_out, stop);
  and and_1 (and_1_out, clock_2_out, not_1_out);
  TTY #(.rows(1), .cols(21)) tty_1 (.data({4'b0110, Q2, Q1, Q0}), .clk(and_1_out), .clr(Reset));  // open: we
  Counter #(.width(5), .max('h14), .ongoal("stay")) counter_1 (
    .carry(stop), .clk(and_1_out), .clr(Reset));  // open: load, D, count, Q
  Counter #(.width(5), .max('h9), .ongoal("stay")) counter_2 (
    .carry(Up_Down), .clk(and_1_out), .clr(Reset));  // open: load, D, count, Q
  Button u_Reset (.out(Reset));

  // Notes on the sheet:
  //   70123456776543210765
endmodule
