// Logisim project bcd.circ as structural Verilog: 1 circuit, main circuit main
module main (
);

  wire a, and_13_out, and_14_out, b, c, clock_1_out, d, e, f, g, not_4_out, nw0, nw0_nw1, nw0_nw2, nw0w1,
       nw0w2, nw1, nw1_nw2, nw1w2, nw2, Reset_out, stop, w0, w0_nw1, w0_nw2, w0w1, w0w2, w1, w1_nw2, w1w2,
       w2, w3;

  and and_1 (w0w1, w0, w1);
  and and_2 (w0w2, w0, w2);
  and and_3 (w1w2, w1, w2);
  not not_1 (nw0, w0);
  not not_2 (nw1, w1);
  not not_3 (nw2, w2);
  and and_4 (w0_nw1, w0, nw1);
  and and_5 (nw0w1, nw0, w1);
  and and_6 (nw0_nw1, nw0, nw1);
  and and_7 (w0_nw2, w0, nw2);
  and and_8 (nw0w2, nw0, w2);
  and and_9 (nw0_nw2, nw0, nw2);
  and and_10 (nw1w2, nw1, w2);
  and and_11 (w1_nw2, w1, nw2);
  and and_12 (nw1_nw2, nw1, nw2);
  _7_Segment_Display u_7_segment_display_1 (.g(g), .f(f), .a(a), .b(b), .e(e), .d(d), .c(c));  // open: dp
  Clock clock_1 (.out(clock_1_out));
  not not_4 (not_4_out, stop);
  // Probe on {w3, w2, w1, w0}
  and and_13 (and_13_out, clock_1_out, not_4_out);
  and and_14 (and_14_out, w2, w0_nw1);
  TTY #(.rows(10), .cols(1)) tty_1 (.data({3'b100, d, c, b, a}), .clk(and_13_out), .clr(Reset_out));  // open: we
  Counter #(.width(4), .max('h9), .ongoal("stay")) counter_1 (
    .Q({w3, w2, w1, w0}), .carry(stop), .clk(and_13_out), .clr(Reset_out));  // open: load, D, count
  TTY #(.rows(10), .cols(1)) tty_2 (.data({4'b0110, g, f, e}), .clk(and_13_out), .clr(Reset_out));  // open: we
  Button Reset (.out(Reset_out));
  or or_1 (a, w1, w3, w0w2, nw0_nw2);
  or or_2 (b, nw2, nw0_nw1, w0w1);
  or or_3 (c, nw1, w0, w2);
  or or_4 (d, w3, nw0w1, w1_nw2, nw0_nw2, and_14_out);
  or or_5 (e, nw0w1, nw0_nw2);
  or or_6 (f, w3, nw0_nw1, nw1w2, nw0w2);
  or or_7 (g, w3, nw0w1, nw1w2, w1_nw2);

  // Notes on the sheet:
  //   O
  //   F
  //   K
  //   O
  //   F
  //   M
  //   M
  //   G
  //   O
  //   3
  //   0
  //   5
  //   4
  //   6
  //   6
  //   7
  //   0
  //   7
endmodule
