// Logisim project alu.circ as structural Verilog: 1 circuit, main circuit main
module main (
);

  wire A0, A1, A2, Ad0, Ad1, Ad2, Ad3, and_1_out, and_3_out, and_4_out, and_5_out, B0, B1, B2, Bit_0, Bit_1,
       Bit_2, C0, C0P0_out, C1, c1_t, C2, c2_t, c3_but_not_needed_RIPPLE_CARRY, CIN, clock_1_out, CP0P1_out,
       G0_out, G0P1_out, G1_out, G2_out, not_1_out, P0_out, P1_out, P2_out, Reset_out, S0, S1, stop;
  wire [2:0] and_2_out, not_2_out, or_1_out;
  wire [11:3] rom_1_data;

  Clock clock_1 (.out(clock_1_out));
  not not_1 (not_1_out, stop);
  // Probe on CIN
  // Probe on {C2, C1, C0}
  and and_1 (and_1_out, clock_1_out, not_1_out);
  assign and_2_out = {B2, B1, B0} & {A2, A1, A0};  // AND_Gate and_2, 3 bits wide
  assign or_1_out = {B2, B1, B0} | {A2, A1, A0};  // OR_Gate or_1, 3 bits wide
  assign not_2_out = ~{A2, A1, A0};  // NOT_Gate not_2, 3 bits wide
  // Probe on {S1, S0}
  TTY #(.rows(1), .cols(10)) tty_1 (.data({4'b0110, C2, C1, C0}), .clk(and_1_out), .clr(Reset_out));  // open: we
  Counter #(.width(4), .max('ha), .ongoal("stay")) counter_1 (
    .Q({Ad3, Ad2, Ad1, Ad0}), .carry(stop), .clk(and_1_out), .clr(Reset_out));  // open: load, D, count
  // Probe on {rom_1_data[11], CIN, S1, S0, rom_1_data[7], B2, B1, B0, rom_1_data[3], A2, A1, A0}
  ROM #(.addrWidth(4), .dataWidth(12)) rom_1 (
    .addr({Ad3, Ad2, Ad1, Ad0}),
    .data({rom_1_data[11], CIN, S1, S0, rom_1_data[7], B2, B1, B0, rom_1_data[3], A2, A1, A0}));  // open: sel
  // Probe on {B2, B1, B0}
  Multiplexer #(.select(2), .width(3)) multiplexer_1 (
    .in0(and_2_out), .in1(or_1_out), .in2(not_2_out), .in3({Bit_2, Bit_1, Bit_0}), .out({C2, C1, C0}),
    .sel({S1, S0}));  // open: en
  // Probe on {A2, A1, A0}
  Button Reset (.out(Reset_out));
  xor P0 (P0_out, A0, B0);
  and G0 (G0_out, B0, A0);
  and C0P0 (C0P0_out, P0_out, CIN);
  or or_2 (c1_t, G0_out, C0P0_out);
  xor xor_1 (Bit_0, P0_out, CIN);
  xor P1 (P1_out, A1, B1);
  and G1 (G1_out, B1, A1);
  and CP0P1 (CP0P1_out, P1_out, P0_out, CIN);
  or or_3 (c2_t, G1_out, CP0P1_out, G0P1_out);
  xor xor_2 (Bit_1, P1_out, c1_t);
  and G0P1 (G0P1_out, P1_out, G0_out);
  xor P2 (P2_out, A2, B2);
  and G2 (G2_out, B2, A2);
  and and_3 (and_3_out, P2_out, P0_out, CIN, P1_out);
  xor xor_3 (Bit_2, P2_out, c2_t);
  and and_4 (and_4_out, G1_out, P2_out);
  and and_5 (and_5_out, P2_out, P1_out, G0_out);
  or or_4 (c3_but_not_needed_RIPPLE_CARRY, G2_out, and_3_out, and_4_out, and_5_out);

  // Notes on the sheet:
  //   adds 48 to make printable
  //   5 & 3, 6 & 2, 5 | 3, 6 | 2, ~5, ~2, 7 + 7 + 0, 5 + 3 + 0, 6 + 4 + 1, 3 + 2 + 1
  //   1276256036
  //   contents of rom_1 (hex, n*v repeats v):
  //   53 62 153 162 205 202 377 353 764 723
endmodule
