// Logisim project cpu.circ as structural Verilog: 5 circuits, main circuit main
module main (
  output [8:0] out_1,
  output [8:0] out_2,
  output [8:0] out_3,
  output [8:0] out_4,
  output [8:0] out_5,
  output [8:0] out_6,
  output [2:0] out_7,
  output [8:0] out_8,
  output [8:0] out_9,
  output [3:0] out_10
);

  wire clock_1_out, comparator_1_lt, counter_1_carry, d_ff_1_q, d_ff_3_qn, d_ff_4_qn, d_ff_5_qn, d_ff_6_qn,
       d_ff_7_qn, decoder_1_out7, halt, nop, not_1_out, not_2_out, Reset, STOP, TClock;
  wire [2:0] Mux_A, Mux_B, Reg_Select;
  wire [3:0] multiplexer_3_out;
  wire [4:0] _5_bit_up_counter, counter_1_q, MSB;
  wire [6:0] adder_1_out, decoder_1_out0, LSB;
  wire [8:0] Data, multiplexer_1_out, multiplexer_2_out;

  not not_1 (not_1_out, STOP);
  Decoder #(.select(3)) decoder_1 (
    .out0(decoder_1_out0[0]), .out1(decoder_1_out0[1]), .out2(decoder_1_out0[2]), .out3(decoder_1_out0[3]),
    .out4(decoder_1_out0[4]), .out5(decoder_1_out0[5]), .out6(decoder_1_out0[6]), .out7(decoder_1_out7),
    .sel(Reg_Select), .en(not_1_out));
  // Probe on decoder_1_out0
  D_Flip_Flop d_ff_1 (.clk(TClock), .D(halt), .Q(d_ff_1_q), .reset(Reset));  // open: Qn, preset, en
  Reg_Bank reg_bank_1 (
    .Decoder_s_Output(decoder_1_out0), .out_5(out_1), .out_6(out_2), .out_7(out_4), .out_8(out_5),
    .out_9(out_6), .out_10(out_8), .out_11(out_9), .Reset(Reset), .Data(out_3), .T_Clock(TClock));
  D_Flip_Flop d_ff_2 (.clk(d_ff_1_q), .D(d_ff_1_q), .Q(STOP), .reset(Reset));  // open: Qn, preset, en
  Multiplexer #(.select(3), .width(9)) multiplexer_1 (
    .in0(out_1), .in1(out_2), .in2(out_4), .in3(out_5), .in4(out_6), .in5(out_8), .in6(out_9),
    .out(multiplexer_1_out), .sel(Mux_A));  // open: in7, en
  ALU alu_1 (
    .Output(out_3), .OpCode(out_10), .in_1(multiplexer_1_out), .in_2(multiplexer_2_out),
    .Instruction_Data(Data), .nop(nop), .halt(halt));
  Multiplexer #(.select(3), .width(9)) multiplexer_2 (
    .in0(out_1), .in1(out_2), .in2(out_4), .in3(out_5), .in4(out_6), .in5(out_8), .in6(out_9),
    .out(multiplexer_2_out), .sel(Mux_B));  // open: in7, en
  TTY #(.rows(33), .cols(1)) tty_1 (.data({2'b10, MSB}), .clk(TClock), .clr(Reset));  // open: we
  TTY #(.rows(33), .cols(1)) tty_2 (.data(LSB), .clk(TClock), .clr(Reset));  // open: we
  Button u_Reset (.out(Reset));
  Counter #(.width(5), .max('h1f), .ongoal("stay")) counter_1 (
    .Q(counter_1_q), .carry(counter_1_carry), .clk(TClock), .clr(Reset));  // open: load, D, count
  Multiplexer #(.select(3), .width(9), .disabled(0), .enable("false")) multiplexer_3 (
    .in0(out_1), .in1(out_2), .in2(out_4), .in3(out_5), .in4(out_6), .in5(out_8), .in6(out_9),
    .out({MSB, multiplexer_3_out}), .sel(out_7));  // open: in7
  not not_2 (not_2_out, counter_1_carry);
  Clock clock_1 (.out(clock_1_out));
  D_Flip_Flop d_ff_3 (
    .clk(TClock), .D(d_ff_3_qn), .Q(_5_bit_up_counter[0]), .Qn(d_ff_3_qn), .reset(Reset));  // open: preset, en
  and and_1 (TClock, not_2_out, clock_1_out);
  ROM #(.addrWidth(5), .dataWidth(3)) rom_1 (.addr(counter_1_q), .data(out_7));  // open: sel
  RAM #(.addrWidth(5), .dataWidth(22)) ram_1 (
    .addr(_5_bit_up_counter), .data({out_10, Mux_A, Mux_B, Reg_Select, Data}), .clk(TClock), .clr(STOP));  // open: sel, ld
  D_Flip_Flop d_ff_4 (
    .clk(d_ff_3_qn), .D(d_ff_4_qn), .Q(_5_bit_up_counter[1]), .Qn(d_ff_4_qn), .reset(Reset));  // open: preset, en
  // Probe on {3'b011, multiplexer_3_out}
  // Probe on {2'b10, MSB}
  D_Flip_Flop d_ff_5 (
    .clk(d_ff_4_qn), .D(d_ff_5_qn), .Q(_5_bit_up_counter[2]), .Qn(d_ff_5_qn), .reset(Reset));  // open: preset, en
  Comparator #(.width(7)) comparator_1 (
    .a(7'b0111001), .b({3'b011, multiplexer_3_out}), .lt(comparator_1_lt));  // open: gt, eq
  D_Flip_Flop d_ff_6 (
    .clk(d_ff_5_qn), .D(d_ff_6_qn), .Q(_5_bit_up_counter[3]), .Qn(d_ff_6_qn), .reset(Reset));  // open: preset, en
  // Probe on LSB
  Multiplexer #(.width(7), .disabled(0), .enable("false")) multiplexer_4 (
    .in0({3'b011, multiplexer_3_out}), .in1(adder_1_out), .out(LSB), .sel(comparator_1_lt));
  Adder #(.width(7)) adder_1 (.a({3'b011, multiplexer_3_out}), .b(7'b0000111), .out(adder_1_out));  // open: cin, cout
  D_Flip_Flop d_ff_7 (
    .clk(d_ff_6_qn), .D(d_ff_7_qn), .Q(_5_bit_up_counter[4]), .Qn(d_ff_7_qn), .reset(Reset));  // open: preset, en

  // Other names for the same wires on the sheet: OpCode[3:0] = out_10; ALU_out[8:0] = out_3; R0[8:0] = out_1;
  //   R1[8:0] = out_2; R2[8:0] = out_4; R3[8:0] = out_5; R4[8:0] = out_6; R5[8:0] = out_8; R6[8:0] = out_9

  // Notes on the sheet:
  //   Christopher Chan (998005560)
  //   @0
  //   JA
  //   E5
  //   @0
  //   OF
  //   U5
  //   OF
  //   E5
  //   E5
  //   U4
  //   E5
  //   E5
  //   U4
  //   _F
  //   _F
  //   _F
  //   AF
  //   AF
  //   AF
  //   @0
  //   AE
  //   AE
  //   AE
  //   _E
  //   OF
  //   ^0
  //   J9
  //   P1
  //   R0
  //   R0
  //   _F
  //   5 Bit Up Counter
  //   contents of rom_1 (hex, n*v repeats v):
  //   0 0 1 2 3 4 5 6 6 2 3 4 5 6 6 0 1 2 3 4 5 6 6 2 3 4 5 6 6 6
endmodule

module ALU (
  input  [8:0] in_1,
  input  [8:0] in_2,
  input  [8:0] Instruction_Data,
  input  [3:0] OpCode,
  output [8:0] Output,
  output halt,
  output nop
);

  wire cla_1_out_11, cla_2_out_11, cla_4_out_11, cla_5_out_11, multiplexer_1_out, multiplexer_2_out,
       multiplexer_3_out, multiplexer_5_out, multiplexer_6_out, multiplexer_7_out, multiplexer_9_out,
       multiplexer_10_out, multiplexer_11_out, multiplexer_13_out, multiplexer_14_out, multiplexer_15_out,
       multiplexer_16_out, multiplexer_17_out, multiplexer_18_out, multiplexer_19_out, multiplexer_20_out,
       multiplexer_21_out, not_2_out, not_3_out, not_4_out, not_5_out, not_6_out, not_7_out, not_8_out,
       not_9_out, not_10_out, not_11_out, not_12_out, not_13_out, not_14_out, not_15_out, not_16_out,
       not_17_out, not_18_out, not_19_out, S0, S1, S2, S3, S4, S5, S6, S7, S8, Si0, Si1, Si2, Si3, Si4, Si5,
       Si6, Si7, Si8;
  wire [8:0] AND, NOT, OR, SLL, SRL;

  assign AND = in_1 & in_2;  // AND_Gate and_1, 9 bits wide
  assign OR = in_1 | in_2;  // OR_Gate or_1, 9 bits wide
  assign NOT = ~in_1;  // NOT_Gate not_1, 9 bits wide
  Shifter #(.width(9)) shifter_1 (.in(in_1), .\dist (4'b0001), .out(SLL));
  Shifter #(.width(9), .shift("lr")) shifter_2 (.in(in_1), .\dist (4'b0001), .out(SRL));
  not not_2 (not_2_out, in_2[0]);
  Multiplexer #(.enable("false")) multiplexer_1 (
    .in0(in_2[0]), .in1(not_2_out), .out(multiplexer_1_out), .sel(OpCode[2]));
  CLA cla_1 (
    .in_1(in_1[0]), .in_2(in_1[1]), .in_3(in_1[2]), .in_4(multiplexer_1_out), .in_5(multiplexer_2_out),
    .in_6(multiplexer_3_out), .out_11(cla_1_out_11), .out_8(S0), .out_9(S1), .out_10(S2), .in_7(OpCode[2]));
  not not_3 (not_3_out, in_2[1]);
  not not_4 (not_4_out, in_2[2]);
  Multiplexer #(.enable("false")) multiplexer_2 (
    .in0(in_2[1]), .in1(not_3_out), .out(multiplexer_2_out), .sel(OpCode[2]));
  Multiplexer #(.enable("false")) multiplexer_3 (
    .in0(in_2[2]), .in1(not_4_out), .out(multiplexer_3_out), .sel(OpCode[2]));
  Multiplexer #(.select(4), .enable("false")) multiplexer_4 (
    .in0(1'b0), .in1(1'b0), .in2(1'b0), .in3(1'b0), .in4(1'b0), .in5(1'b0), .in6(1'b0), .in7(1'b0),
    .in8(1'b0), .in9(1'b0), .in10(1'b0), .in11(1'b0), .in15(1'b1), .out(halt), .sel(OpCode));  // open: in12, in13, in14
  CLA cla_2 (
    .in_1(in_1[3]), .in_2(in_1[4]), .in_3(in_1[5]), .in_4(multiplexer_6_out), .in_5(multiplexer_5_out),
    .in_6(multiplexer_7_out), .out_11(cla_2_out_11), .out_8(S3), .out_9(S4), .out_10(S5), .in_7(cla_1_out_11));
  not not_5 (not_5_out, in_2[4]);
  not not_6 (not_6_out, in_2[3]);
  Multiplexer #(.enable("false")) multiplexer_5 (
    .in0(in_2[4]), .in1(not_5_out), .out(multiplexer_5_out), .sel(OpCode[2]));
  Multiplexer #(.enable("false")) multiplexer_6 (
    .in0(in_2[3]), .in1(not_6_out), .out(multiplexer_6_out), .sel(OpCode[2]));
  not not_7 (not_7_out, in_2[5]);
  Multiplexer #(.enable("false")) multiplexer_7 (
    .in0(in_2[5]), .in1(not_7_out), .out(multiplexer_7_out), .sel(OpCode[2]));
  Multiplexer #(.select(4), .enable("false")) multiplexer_8 (
    .in0(1'b0), .in1(1'b0), .in2(1'b0), .in3(1'b0), .in4(1'b0), .in5(1'b0), .in6(1'b0), .in7(1'b0),
    .in8(1'b0), .in9(1'b0), .in10(1'b0), .in11(1'b1), .out(nop), .sel(OpCode));  // open: in12, in13, in14, in15
  Multiplexer #(.enable("false")) multiplexer_9 (
    .in0(in_2[6]), .in1(not_9_out), .out(multiplexer_9_out), .sel(OpCode[2]));
  CLA cla_3 (
    .in_1(in_1[6]), .in_2(in_1[7]), .in_3(in_1[8]), .in_4(multiplexer_9_out), .in_5(multiplexer_11_out),
    .in_6(multiplexer_10_out), .out_8(S6), .out_9(S7), .out_10(S8), .in_7(cla_2_out_11));  // open: out_11
  not not_8 (not_8_out, in_2[7]);
  not not_9 (not_9_out, in_2[6]);
  Multiplexer #(.enable("false")) multiplexer_10 (
    .in0(in_2[8]), .in1(not_10_out), .out(multiplexer_10_out), .sel(OpCode[2]));
  Multiplexer #(.enable("false")) multiplexer_11 (
    .in0(in_2[7]), .in1(not_8_out), .out(multiplexer_11_out), .sel(OpCode[2]));
  Multiplexer #(.select(4), .width(9), .enable("false")) multiplexer_12 (
    .in0(AND), .in1(OR), .in2(NOT), .in3({S8, S7, S6, S5, S4, S3, S2, S1, S0}), .in4(in_1), .in5(SLL),
    .in6(SRL), .in7({S8, S7, S6, S5, S4, S3, S2, S1, S0}),
    .in8({Si8, Si7, Si6, Si5, Si4, Si3, Si2, Si1, Si0}), .in9({Si8, Si7, Si6, Si5, Si4, Si3, Si2, Si1, Si0}),
    .in10(Instruction_Data), .in11(in_1), .in15(in_1), .out(Output), .sel(OpCode));  // open: in12, in13, in14
  not not_10 (not_10_out, in_2[8]);
  CLA cla_4 (
    .in_1(in_1[0]), .in_2(in_1[1]), .in_3(in_1[2]), .in_4(multiplexer_14_out), .in_5(multiplexer_13_out),
    .in_6(multiplexer_15_out), .out_11(cla_4_out_11), .out_8(Si0), .out_9(Si1), .out_10(Si2), .in_7(OpCode[0]));
  not not_11 (not_11_out, Instruction_Data[1]);
  not not_12 (not_12_out, Instruction_Data[0]);
  Multiplexer #(.enable("false")) multiplexer_13 (
    .in0(Instruction_Data[1]), .in1(not_11_out), .out(multiplexer_13_out), .sel(OpCode[0]));
  Multiplexer #(.enable("false")) multiplexer_14 (
    .in0(Instruction_Data[0]), .in1(not_12_out), .out(multiplexer_14_out), .sel(OpCode[0]));
  not not_13 (not_13_out, Instruction_Data[2]);
  Multiplexer #(.enable("false")) multiplexer_15 (
    .in0(Instruction_Data[2]), .in1(not_13_out), .out(multiplexer_15_out), .sel(OpCode[0]));
  not not_14 (not_14_out, Instruction_Data[3]);
  Multiplexer #(.enable("false")) multiplexer_16 (
    .in0(Instruction_Data[3]), .in1(not_14_out), .out(multiplexer_16_out), .sel(OpCode[0]));
  CLA cla_5 (
    .in_1(in_1[3]), .in_2(in_1[4]), .in_3(in_1[5]), .in_4(multiplexer_16_out), .in_5(multiplexer_18_out),
    .in_6(multiplexer_17_out), .out_11(cla_5_out_11), .out_8(Si3), .out_9(Si4), .out_10(Si5),
    .in_7(cla_4_out_11));
  not not_15 (not_15_out, Instruction_Data[4]);
  not not_16 (not_16_out, Instruction_Data[5]);
  Multiplexer #(.enable("false")) multiplexer_17 (
    .in0(Instruction_Data[5]), .in1(not_16_out), .out(multiplexer_17_out), .sel(OpCode[0]));
  Multiplexer #(.enable("false")) multiplexer_18 (
    .in0(Instruction_Data[4]), .in1(not_15_out), .out(multiplexer_18_out), .sel(OpCode[0]));
  CLA cla_6 (
    .in_1(in_1[6]), .in_2(in_1[7]), .in_3(in_1[8]), .in_4(multiplexer_19_out), .in_5(multiplexer_20_out),
    .in_6(multiplexer_21_out), .out_8(Si6), .out_9(Si7), .out_10(Si8), .in_7(cla_5_out_11));  // open: out_11
  not not_17 (not_17_out, Instruction_Data[6]);
  not not_18 (not_18_out, Instruction_Data[7]);
  Multiplexer #(.enable("false")) multiplexer_19 (
    .in0(Instruction_Data[6]), .in1(not_17_out), .out(multiplexer_19_out), .sel(OpCode[0]));
  Multiplexer #(.enable("false")) multiplexer_20 (
    .in0(Instruction_Data[7]), .in1(not_18_out), .out(multiplexer_20_out), .sel(OpCode[0]));
  not not_19 (not_19_out, Instruction_Data[8]);
  Multiplexer #(.enable("false")) multiplexer_21 (
    .in0(Instruction_Data[8]), .in1(not_19_out), .out(multiplexer_21_out), .sel(OpCode[0]));

  // Other names for the same wires on the sheet: B0 = in_2[0]; B1 = in_2[1]; B2 = in_2[2]; B3 = in_2[3]; B4 = in_2[4];
  //   B5 = in_2[5]; B6 = in_2[6]; B7 = in_2[7]; B8 = in_2[8]; i0 = Instruction_Data[0]; i1 = Instruction_Data[1];
  //   i2 = Instruction_Data[2]; i3 = Instruction_Data[3]; i4 = Instruction_Data[4]; i5 = Instruction_Data[5];
  //   i6 = Instruction_Data[6]; i7 = Instruction_Data[7]; i8 = Instruction_Data[8]; A0 = in_1[0]; MOV[8:0] = in_1;
  //   NOP_t[8:0] = in_1; A1 = in_1[1]; A2 = in_1[2]; A3 = in_1[3]; A4 = in_1[4]; A5 = in_1[5]; A6 = in_1[6];
  //   A7 = in_1[7]; A8 = in_1[8]; add_sub_i = OpCode[0]; add_sub = OpCode[2]

  // Notes on the sheet:
  //   A
  //   B
endmodule

module CLA (
  input  in_1,
  input  in_2,
  input  in_3,
  input  in_4,
  input  in_5,
  input  in_6,
  input  in_7,
  output out_8,
  output out_9,
  output out_10,
  output out_11
);

  wire and_1_out, and_2_out, and_3_out, C0P0_out, c1, c2, CP0P1_out, G0_out, G0P1_out, G1_out, G2_out,
       P0_out, P1_out, P2_out;

  xor P0 (P0_out, in_1, in_4);
  and G0 (G0_out, in_4, in_1);
  and C0P0 (C0P0_out, P0_out, in_7);
  or or_1 (c1, G0_out, C0P0_out);
  xor xor_1 (out_8, P0_out, in_7);
  and G1 (G1_out, in_5, in_2);
  xor P1 (P1_out, in_2, in_5);
  and CP0P1 (CP0P1_out, P1_out, P0_out, in_7);
  and G0P1 (G0P1_out, P1_out, G0_out);
  or or_2 (c2, G1_out, CP0P1_out, G0P1_out);
  xor xor_2 (out_9, P1_out, c1);
  xor P2 (P2_out, in_3, in_6);
  and G2 (G2_out, in_6, in_3);
  xor xor_3 (out_10, P2_out, c2);
  and and_1 (and_1_out, P2_out, P0_out, in_7, P1_out);
  and and_2 (and_2_out, G1_out, P2_out);
  or or_3 (out_11, G2_out, and_1_out, and_2_out, and_3_out);
  and and_3 (and_3_out, P2_out, P1_out, G0_out);
endmodule

module Reg_Bank (
  input  T_Clock,
  input  [8:0] Data,
  input  Reset,
  input  [6:0] Decoder_s_Output,
  output [8:0] out_5,
  output [8:0] out_6,
  output [8:0] out_7,
  output [8:0] out_8,
  output [8:0] out_9,
  output [8:0] out_10,
  output [8:0] out_11
);

  Register register_1 (
    .T_Clock(T_Clock), .Data_to_write(Data), .out_5(out_5), .Enable(Decoder_s_Output[0]), .Reset(Reset));
  Register register_2 (
    .T_Clock(T_Clock), .Data_to_write(Data), .out_5(out_6), .Enable(Decoder_s_Output[1]), .Reset(Reset));
  Register register_3 (
    .T_Clock(T_Clock), .Data_to_write(Data), .out_5(out_7), .Enable(Decoder_s_Output[2]), .Reset(Reset));
  Register register_4 (
    .T_Clock(T_Clock), .Data_to_write(Data), .out_5(out_8), .Enable(Decoder_s_Output[3]), .Reset(Reset));
  Register register_5 (
    .T_Clock(T_Clock), .Data_to_write(Data), .out_5(out_9), .Enable(Decoder_s_Output[4]), .Reset(Reset));
  Register register_6 (
    .T_Clock(T_Clock), .Data_to_write(Data), .out_5(out_10), .Enable(Decoder_s_Output[5]), .Reset(Reset));
  Register register_7 (
    .T_Clock(T_Clock), .Data_to_write(Data), .out_5(out_11), .Enable(Decoder_s_Output[6]), .Reset(Reset));
endmodule

module Register (
  input  T_Clock,
  input  Enable,
  input  Reset,
  input  [8:0] Data_to_write,
  output [8:0] out_5
);

  D_Flip_Flop d_ff_1 (
    .clk(T_Clock), .D(Data_to_write[0]), .Q(out_5[0]), .en(Enable), .reset(Reset));  // open: Qn, preset
  D_Flip_Flop d_ff_2 (
    .clk(T_Clock), .D(Data_to_write[1]), .Q(out_5[1]), .en(Enable), .reset(Reset));  // open: Qn, preset
  D_Flip_Flop d_ff_3 (
    .clk(T_Clock), .D(Data_to_write[2]), .Q(out_5[2]), .en(Enable), .reset(Reset));  // open: Qn, preset
  D_Flip_Flop d_ff_4 (
    .clk(T_Clock), .D(Data_to_write[3]), .Q(out_5[3]), .en(Enable), .reset(Reset));  // open: Qn, preset
  D_Flip_Flop d_ff_5 (
    .clk(T_Clock), .D(Data_to_write[4]), .Q(out_5[4]), .en(Enable), .reset(Reset));  // open: Qn, preset
  D_Flip_Flop d_ff_6 (
    .clk(T_Clock), .D(Data_to_write[5]), .Q(out_5[5]), .en(Enable), .reset(Reset));  // open: Qn, preset
  D_Flip_Flop d_ff_7 (
    .clk(T_Clock), .D(Data_to_write[6]), .Q(out_5[6]), .en(Enable), .reset(Reset));  // open: Qn, preset
  D_Flip_Flop d_ff_8 (
    .clk(T_Clock), .D(Data_to_write[7]), .Q(out_5[7]), .en(Enable), .reset(Reset));  // open: Qn, preset
  D_Flip_Flop d_ff_9 (
    .clk(T_Clock), .D(Data_to_write[8]), .Q(out_5[8]), .en(Enable), .reset(Reset));  // open: Qn, preset
endmodule
