// Logisim project sec.circ as structural Verilog: 1 circuit, main circuit main
module main (
);

  wire A0, A1, A2, C0, C1, C2, C3, CC0, CC1, CC2, CC3, clock_1_out, go, P0, P1, P2, Reset_out, t_ff_1_q,
       t_ff_2_q, t_ff_3_q, t_ff_4_q, t_ff_5_q, t_ff_6_q, Z0, Z1, Z2, Z3, Z4, Z5, Z6, Z7;
  wire [0:0] multiplexer_1_out;
  wire [1:0] _1_flipped;
  wire [2:2] _2_flipped;
  wire [3:0] xor_1_out;
  wire [3:3] _3_flipped;
  wire [4:4] _4_flipped;
  wire [5:5] _5_flipped;
  wire [6:6] _6_flipped;
  wire [7:0] _0_flipped;
  wire [7:7] _7_flipped;

  Clock clock_1 (.out(clock_1_out));
  T_Flip_Flop t_ff_1 (.clk(clock_1_out), .T(1'b1), .Q(t_ff_1_q), .Qn(P0), .preset(Reset_out), .en(go));  // open: reset
  xor xor_1 (xor_1_out[0], C0, CC0);
  xor xor_2 (xor_1_out[1], C1, CC1);
  xor xor_3 (xor_1_out[2], C2, CC2);
  xor xor_4 (xor_1_out[3], C3, CC3);
  Multiplexer #(.select(3), .disabled(0), .enable("false")) multiplexer_1 (
    .in0(Z7), .in1(Z6), .in2(Z5), .in3(Z4), .in4(Z3), .in5(Z2), .in6(Z1), .in7(Z0),
    .out(multiplexer_1_out[0]), .sel({P2, P1, P0}));
  T_Flip_Flop t_ff_2 (.clk(t_ff_1_q), .T(1'b1), .Q(t_ff_2_q), .Qn(P1), .preset(Reset_out));  // open: reset, en
  Multiplexer #(.select(4), .width(8), .enable("false")) multiplexer_2 (
    .in0({_0_flipped[7:1], _1_flipped[0]}), .in1({_0_flipped[7:1], _1_flipped[0]}),
    .in2({_0_flipped[7:1], _1_flipped[0]}), .in3(_0_flipped), .in4({_0_flipped[7:1], _1_flipped[0]}),
    .in5({_0_flipped[7:2], _1_flipped}),
    .in6({_0_flipped[7:3], _2_flipped[2], _0_flipped[1], _1_flipped[0]}),
    .in7({_0_flipped[7:4], _3_flipped[3], _0_flipped[2:1], _1_flipped[0]}),
    .in8({_0_flipped[7:1], _1_flipped[0]}),
    .in9({_0_flipped[7:5], _4_flipped[4], _0_flipped[3:1], _1_flipped[0]}),
    .in10({_0_flipped[7:6], _5_flipped[5], _0_flipped[4:1], _1_flipped[0]}),
    .in11({_0_flipped[7], _6_flipped[6], _0_flipped[5:1], _1_flipped[0]}),
    .in12({_7_flipped[7], _0_flipped[6:1], _1_flipped[0]}), .out({Z7, Z6, Z5, Z4, Z3, Z2, Z1, Z0}),
    .sel(xor_1_out));  // open: in13, in14, in15
  T_Flip_Flop t_ff_3 (.clk(t_ff_2_q), .T(1'b1), .Q(t_ff_3_q), .Qn(P2), .preset(Reset_out));  // open: reset, en
  ROM #(.addrWidth(3), .dataWidth(12)) rom_1 (
    .addr({A2, A1, A0}), .data({_0_flipped[7:4], C3, _0_flipped[3:1], C2, _1_flipped[0], C1, C0}));  // open: sel
  xor odd_parity_1 (CC0, _0_flipped[1], _1_flipped[0], _0_flipped[3], _0_flipped[4], _0_flipped[6]);
  xor odd_parity_2 (CC1, _1_flipped[0], _0_flipped[2], _0_flipped[3], _0_flipped[5], _0_flipped[6]);
  xor odd_parity_3 (CC2, _0_flipped[1], _0_flipped[2], _0_flipped[3], _0_flipped[7]);
  xor odd_parity_4 (CC3, _0_flipped[4], _0_flipped[5], _0_flipped[6], _0_flipped[7]);
  TTY #(.cols(8)) tty_1 (.data({6'b011000, multiplexer_1_out[0]}), .clk(clock_1_out), .we(go), .clr(Reset_out));
  T_Flip_Flop t_ff_4 (.clk(t_ff_3_q), .T(1'b1), .Q(t_ff_4_q), .Qn(A0), .preset(Reset_out));  // open: reset, en
  // Probe on {_0_flipped[7:4], C3, _0_flipped[3:1], C2, _1_flipped[0], C1, C0}
  T_Flip_Flop t_ff_5 (.clk(t_ff_4_q), .T(1'b1), .Q(t_ff_5_q), .Qn(A1), .preset(Reset_out));  // open: reset, en
  T_Flip_Flop t_ff_6 (.clk(t_ff_5_q), .T(1'b1), .Q(t_ff_6_q), .Qn(A2), .preset(Reset_out));  // open: reset, en
  Button Reset (.out(Reset_out));
  T_Flip_Flop t_ff_7 (.clk(t_ff_6_q), .T(1'b1), .Q(go), .preset(Reset_out));  // open: Qn, reset, en
  not not_1 (_0_flipped[0], _1_flipped[0]);
  not not_2 (_1_flipped[1], _0_flipped[1]);
  not not_3 (_2_flipped[2], _0_flipped[2]);
  not not_4 (_3_flipped[3], _0_flipped[3]);
  not not_5 (_4_flipped[4], _0_flipped[4]);
  not not_6 (_5_flipped[5], _0_flipped[5]);
  not not_7 (_6_flipped[6], _0_flipped[6]);
  not not_8 (_7_flipped[7], _0_flipped[7]);

  // Other names for the same wires on the sheet: _1_flipped[7:2] = _0_flipped[7:2];
  //   _2_flipped (some bits) = {_0_flipped[7:3], _0_flipped[1], _1_flipped[0]};
  //   _3_flipped (some bits) = {_0_flipped[7:4], _0_flipped[2:1], _1_flipped[0]};
  //   _4_flipped (some bits) = {_0_flipped[7:5], _0_flipped[3:1], _1_flipped[0]};
  //   _5_flipped (some bits) = {_0_flipped[7:6], _0_flipped[4:1], _1_flipped[0]};
  //   _6_flipped (some bits) = {_0_flipped[7], _0_flipped[5:1], _1_flipped[0]};
  //   all_G[7:0] = {_0_flipped[7:1], _1_flipped[0]}; D7 = _0_flipped[7];
  //   _7_flipped[6:0] = {_0_flipped[6:1], _1_flipped[0]}; D0 = _1_flipped[0]; D1 = _0_flipped[1]; D2 = _0_flipped[2];
  //   D3 = _0_flipped[3]; D4 = _0_flipped[4]; D5 = _0_flipped[5]; D6 = _0_flipped[6]

  // Notes on the sheet:
  //   contents of rom_1 (hex, n*v repeats v):
  //   d7 788 a75 a74 275 b75 f75 a77
  //   00101011
  //   01110000
  //   10101111
  //   10101111
  //   10101111
  //   10101111
  //   11111111
  //   10101111
endmodule
