// Logisim project IO-device.circ as structural Verilog: 1 circuit, main circuit main
module main (
  input  WrEn
);

  wire clock_1_out;
  wire [31:0] adder_1_out, fetch_addr, Instruction, main_1_s0_value, register_1_q;

  cpu_main main_1 (
    .INSTRUCTION(Instruction), .CLOCK(clock_1_out), .FETCH_ADDRESS(fetch_addr), .s0_Value(main_1_s0_value));  // open: s1_Value, s2_Value, ra_Value, sp_Value
  Clock clock_1 (.out(clock_1_out));
  Adder #(.width(32)) adder_1 (.a(register_1_q), .b(main_1_s0_value), .out(adder_1_out));  // open: cin, cout
  Register #(.width(32)) register_1 (.D(adder_1_out), .en(WrEn), .Q(register_1_q), .clk(clock_1_out));  // open: clr
  // Probe on fetch_addr
  Hex_Digit_Display hex_digit_display_1 (.value(register_1_q[27:24]));  // open: dp
  Hex_Digit_Display hex_digit_display_2 (.value(register_1_q[31:28]));  // open: dp
  Hex_Digit_Display hex_digit_display_3 (.value(register_1_q[23:20]));  // open: dp
  Hex_Digit_Display hex_digit_display_4 (.value(register_1_q[19:16]));  // open: dp
  Hex_Digit_Display hex_digit_display_5 (.value(register_1_q[15:12]));  // open: dp
  Hex_Digit_Display hex_digit_display_6 (.value(register_1_q[11:8]));  // open: dp
  ROM #(.addrWidth(24), .dataWidth(32)) rom_1 (.addr(fetch_addr[25:2]), .data(Instruction));  // open: sel
  Hex_Digit_Display hex_digit_display_7 (.value(register_1_q[3:0]));  // open: dp
  Hex_Digit_Display hex_digit_display_8 (.value(register_1_q[7:4]));  // open: dp
  // Probe on Instruction

  // Notes on the sheet:
  //   If the write address is equal to 00007f00 the write data will be added to the current value of the hex display
  //   Instruction Memory
  //   contents of rom_1 (hex, n*v repeats v):
  //   20100000 3c010098 34219680 18820 12110002 22100002 8000004
endmodule
