// Logisim project cpu.circ as structural Verilog
module main (
  input  [31:0] INSTRUCTION,
  input  CLOCK,
  output [31:0] FETCH_ADDRESS,
  output [31:0] s0_Value,
  output [31:0] s1_Value,
  output [31:0] s2_Value,
  output [31:0] ra_Value,
  output [31:0] sp_Value
);

  wire ALUSrc, and_2_out, and_3_out, and_4_out, and_5_out, bgezal, Branch, comparator_1_eq, comparator_1_gt,
       doBranch, jr, Jump, main_2_p3, main_2_p5, main_2_p8, main_2_p13, MemRead, MemtoReg, MEMWrite,
       not_1_out, not_2_out, not_3_out, not_4_out, not_5_out, not_6_out, not_7_out, not_8_out, not_9_out,
       not_10_out, not_11_out, not_12_out, not_13_out, not_14_out, not_15_out, or_1_out, RegDst, RegWrite;
  wire [0:0] or_3_out;
  wire [3:0] ALUOP;
  wire [4:0] adder_2_out, multiplexer_2_out, multiplexer_3_out, multiplexer_5_out, to_ra;
  wire [25:0] shifter_1_out;
  wire [27:0] bit_extender_2_out;
  wire [31:0] adder_3_out, imm, main_2_p7, main_2_p15, multiplexer_1_out, multiplexer_4_out,
       multiplexer_6_out, multiplexer_7_out, multiplexer_8_out, multiplexer_9_out, multiplexer_10_out,
       multiplexer_11_out, pc_4, ra_t, toRAM;

  Multiplexer #(.width(32)) multiplexer_1 (
    .in0(multiplexer_10_out), .in1(ra_Value), .out(multiplexer_1_out), .sel(jr));  // open: en
  Register #(.width(32)) PC (.D(multiplexer_1_out), .Q(FETCH_ADDRESS), .clk(CLOCK));  // open: en, clr
  Adder #(.width(32)) adder_1 (.a(FETCH_ADDRESS), .b(32'h4), .out(pc_4));  // open: cin, cout
  Control control_1 (
    .in_1(INSTRUCTION[31:26]), .RegDst(RegDst), .Jump(Jump), .Branch(Branch), .MemRead(MemRead),
    .MemtoReg(MemtoReg), .MemWrite(MEMWrite), .ALUSrc(ALUSrc), .RegWrite(RegWrite));
  Adder #(.width(5)) adder_2 (.a(INSTRUCTION[20:16]), .b(to_ra), .out(adder_2_out));  // open: cin, cout
  Shifter #(.width(26)) shifter_1 (.in(INSTRUCTION[25:0]), .\dist (5'b00010), .out(shifter_1_out));
  not not_1 (not_1_out, INSTRUCTION[0]);
  not not_2 (not_2_out, INSTRUCTION[1]);
  not not_3 (not_3_out, INSTRUCTION[2]);
  and and_1 (jr, not_1_out, not_2_out, not_3_out, INSTRUCTION[3], not_4_out, not_5_out);
  not not_4 (not_4_out, INSTRUCTION[4]);
  not not_5 (not_5_out, INSTRUCTION[5]);
  Multiplexer #(.width(5)) multiplexer_2 (
    .in0(multiplexer_3_out), .in1({5{1'b1}}), .out(multiplexer_2_out), .sel(doBranch));  // open: en
  Multiplexer #(.width(5)) multiplexer_3 (
    .in0(adder_2_out), .in1(INSTRUCTION[15:11]), .out(multiplexer_3_out), .sel(RegDst));  // open: en
  assign imm = {{16{1'b0}}, INSTRUCTION[15:0]};  // Bit_Extender bit_extender_1
  Multiplexer #(.width(32)) multiplexer_4 (
    .in0(imm), .in1(pc_4), .out(multiplexer_4_out), .sel(and_5_out));  // open: en
  assign bit_extender_2_out = {{2{1'b0}}, shifter_1_out};  // Bit_Extender bit_extender_2
  Multiplexer #(.width(5)) multiplexer_5 (
    .in0(INSTRUCTION[25:21]), .in1({5{1'b1}}), .out(multiplexer_5_out), .sel(jr));  // open: en
  Multiplexer #(.width(32)) multiplexer_6 (
    .in0(multiplexer_11_out), .in1(pc_4), .out(multiplexer_6_out), .sel(doBranch));  // open: en
  \reg  regfile (
    .Read_Register_1(multiplexer_5_out), .Read_Register_2(adder_2_out), .Write_Register(multiplexer_2_out),
    .Write_Data(multiplexer_6_out), .Write_Enable(RegWrite), .Clock(CLOCK), .s0_Value(s0_Value),
    .s1_Value(s1_Value), .s2_Value(s2_Value), .ra_Value(ra_Value), .sp_Value(sp_Value), .Read_Data_1(ra_t),
    .Read_Data_2(toRAM));
  Multiplexer #(.width(32)) multiplexer_7 (
    .in0(multiplexer_4_out), .in1(pc_4), .out(multiplexer_7_out), .sel(bgezal));  // open: en
  Multiplexer #(.width(32)) multiplexer_8 (
    .in0(toRAM), .in1(multiplexer_7_out), .out(multiplexer_8_out), .sel(ALUSrc));  // open: en
  Adder #(.width(32)) adder_3 (.a(imm), .b(pc_4), .out(adder_3_out));  // open: cin, cout
  // alu_main main_1: pin names not known
  Multiplexer #(.width(32)) multiplexer_9 (
    .in0(pc_4), .in1(adder_3_out), .out(multiplexer_9_out), .sel(Branch));  // open: en
  Comparator #(.width(32)) comparator_1 (
    .a(ra_t), .b({32{1'b0}}), .gt(comparator_1_gt), .eq(comparator_1_eq));  // open: lt
  Multiplexer #(.width(32)) multiplexer_10 (
    .in0(multiplexer_9_out), .in1({pc_4[31:28], bit_extender_2_out}), .out(multiplexer_10_out), .sel(Jump));  // open: en
  and and_2 (and_2_out, Branch, or_1_out);
  or or_1 (or_1_out, comparator_1_gt, comparator_1_eq);
  not not_6 (not_6_out, main_2_p5);
  not not_7 (not_7_out, INSTRUCTION[28]);
  not not_8 (not_8_out, INSTRUCTION[29]);
  not not_9 (not_9_out, INSTRUCTION[30]);
  not not_10 (not_10_out, INSTRUCTION[31]);
  not not_11 (not_11_out, INSTRUCTION[27]);
  not not_12 (not_12_out, INSTRUCTION[28]);
  not not_13 (not_13_out, INSTRUCTION[29]);
  not not_14 (not_14_out, INSTRUCTION[30]);
  not not_15 (not_15_out, INSTRUCTION[31]);
  and and_3 (and_3_out, Branch, main_2_p5);
  and and_4 (and_4_out, not_6_out, Branch);
  // mem_main main_2: pin names not known; wires that end beside it: ra_t, multiplexer_8_out, main_2_p3, ALUOP, main_2_p5, main_2_p3, main_2_p7, main_2_p8, main_2_p8, main_2_p7, toRAM, MEMWrite, main_2_p13, CLOCK, main_2_p15
  ALUOp aluop_1 (.funct(INSTRUCTION[5:0]), .Opcode(INSTRUCTION[31:26]), .ALUOp(ALUOP));
  and and_5 (and_5_out, INSTRUCTION[26], INSTRUCTION[27], not_7_out, not_8_out, not_9_out, not_10_out);
  and and_6 (bgezal, INSTRUCTION[26], not_11_out, not_12_out, not_13_out, not_14_out, not_15_out);
  or or_2 (doBranch, and_2_out, and_3_out, and_4_out);
  or or_3 (or_3_out[0], and_5_out, bgezal);
  Multiplexer #(.width(32)) multiplexer_11 (
    .in0(main_2_p7), .in1(main_2_p15), .out(multiplexer_11_out), .sel(MemtoReg));  // open: en
  Multiplier #(.width(5)) multiplier_1 (.a({4'b0000, or_3_out[0]}), .b({5{1'b1}}), .out(to_ra));  // open: cin, cout

  // Other names for the same wires on the sheet: clk = CLOCK; fetch_addr[31:0] = FETCH_ADDRESS;
  //   funct[5:0] = INSTRUCTION[5:0]; opcode[5:0] = INSTRUCTION[31:26]; ra[31:0] = ra_Value; s0[31:0] = s0_Value;
  //   s1[31:0] = s1_Value; s2[31:0] = s2_Value; sp[31:0] = sp_Value

  // Notes on the sheet:
  //   Output
  //   These are outputs/inputs from run.circ
  //   Inputs
  //   control goes here
  //   opcode
  //   RS
  //   RT
  //   RD
  //   IMM
  //   sll2
  //   These are DEBUG/TEST outputs from your circuit.
  //   bgezal
  //   jal
  //   bgezal
  //   beq
  //   bne
endmodule

module \reg  (
  input  [4:0] Read_Register_1,
  input  [4:0] Read_Register_2,
  input  [4:0] Write_Register,
  input  [31:0] Write_Data,
  input  Write_Enable,
  input  Clock,
  output [31:0] s0_Value,
  output [31:0] s1_Value,
  output [31:0] s2_Value,
  output [31:0] ra_Value,
  output [31:0] sp_Value,
  output [31:0] Read_Data_1,
  output [31:0] Read_Data_2
);

  wire _1, _2, _3, _4, _5, _6, _7, _8, _9, _10, _11, _12, _13, _14, _15, _16, _17, _18, _19, _20, _21, _22,
       _23, _24, _25, _26, _27, _28, _29, _30, _31, _32;
  wire [31:0] a0, a1, a2, a3, at, fp, gp, k0, k1, multiplexer_2_out, multiplexer_3_out, multiplexer_4_out,
       multiplexer_5_out, multiplexer_6_out, multiplexer_7_out, multiplexer_8_out, multiplexer_9_out,
       multiplexer_10_out, multiplexer_11_out, multiplexer_12_out, multiplexer_13_out, multiplexer_14_out,
       multiplexer_15_out, multiplexer_16_out, multiplexer_17_out, multiplexer_18_out, multiplexer_19_out,
       multiplexer_20_out, multiplexer_21_out, multiplexer_22_out, multiplexer_23_out, multiplexer_24_out,
       multiplexer_25_out, multiplexer_26_out, multiplexer_27_out, multiplexer_28_out, multiplexer_29_out,
       multiplexer_30_out, multiplexer_31_out, multiplexer_32_out, multiplexer_33_out, s3, s4, s5, s6, s7,
       t0, t1, t2, t3, t4, t5, t6, t7, t8, t9, v0, v1, zero;

  Multiplexer #(.select(5), .width(32)) multiplexer_1 (
    .in0(zero), .in1(at), .in2(v0), .in3(v1), .in4(a0), .in5(a1), .in6(a2), .in7(a3), .in8(t0), .in9(t1),
    .in10(t2), .in11(t3), .in12(t4), .in13(t5), .in14(t6), .in15(t7), .in16(s0_Value), .in17(s1_Value),
    .in18(s2_Value), .in19(s3), .in20(s4), .in21(s5), .in22(s6), .in23(s7), .in24(t8), .in25(t8), .in26(k0),
    .in27(k1), .in28(gp), .in29(sp_Value), .in30(fp), .in31(ra_Value), .out(Read_Data_1),
    .sel(Read_Register_1));  // open: en
  Multiplexer #(.width(32)) multiplexer_2 (.in0(at), .in1(Write_Data), .out(multiplexer_2_out), .sel(_2));  // open: en
  Multiplexer #(.width(32)) multiplexer_3 (.in0(v0), .in1(Write_Data), .out(multiplexer_3_out), .sel(_3));  // open: en
  Multiplexer #(.width(32)) multiplexer_4 (.in0(v1), .in1(Write_Data), .out(multiplexer_4_out), .sel(_4));  // open: en
  Multiplexer #(.width(32)) multiplexer_5 (.in0(a0), .in1(Write_Data), .out(multiplexer_5_out), .sel(_5));  // open: en
  Multiplexer #(.width(32)) multiplexer_6 (.in0(a1), .in1(Write_Data), .out(multiplexer_6_out), .sel(_6));  // open: en
  Multiplexer #(.width(32)) multiplexer_7 (.in0(a2), .in1(Write_Data), .out(multiplexer_7_out), .sel(_7));  // open: en
  Multiplexer #(.width(32)) multiplexer_8 (.in0(a3), .in1(Write_Data), .out(multiplexer_8_out), .sel(_8));  // open: en
  Multiplexer #(.width(32)) multiplexer_9 (.in0(t0), .in1(Write_Data), .out(multiplexer_9_out), .sel(_9));  // open: en
  Multiplexer #(.width(32)) multiplexer_10 (
    .in0(t1), .in1(Write_Data), .out(multiplexer_10_out), .sel(_10));  // open: en
  Multiplexer #(.width(32)) multiplexer_11 (.in0(zero), .out(multiplexer_11_out), .sel(_1));  // open: in1, en
  Register #(.width(32)) register_1 (.D(multiplexer_11_out), .Q(zero), .clk(Clock));  // open: en, clr
  Register #(.width(32)) register_2 (.D(multiplexer_2_out), .Q(at), .clk(Clock));  // open: en, clr
  Register #(.width(32)) register_3 (.D(multiplexer_3_out), .Q(v0), .clk(Clock));  // open: en, clr
  Register #(.width(32)) register_4 (.D(multiplexer_4_out), .Q(v1), .clk(Clock));  // open: en, clr
  Register #(.width(32)) register_5 (.D(multiplexer_5_out), .Q(a0), .clk(Clock));  // open: en, clr
  Register #(.width(32)) register_6 (.D(multiplexer_6_out), .Q(a1), .clk(Clock));  // open: en, clr
  Register #(.width(32)) register_7 (.D(multiplexer_7_out), .Q(a2), .clk(Clock));  // open: en, clr
  Register #(.width(32)) register_8 (.D(multiplexer_8_out), .Q(a3), .clk(Clock));  // open: en, clr
  Register #(.width(32)) register_9 (.D(multiplexer_9_out), .Q(t0), .clk(Clock));  // open: en, clr
  Register #(.width(32)) register_10 (.D(multiplexer_10_out), .Q(t1), .clk(Clock));  // open: en, clr
  Multiplexer #(.width(32)) multiplexer_12 (
    .in0(t2), .in1(Write_Data), .out(multiplexer_12_out), .sel(_11));  // open: en
  Multiplexer #(.width(32)) multiplexer_13 (
    .in0(t3), .in1(Write_Data), .out(multiplexer_13_out), .sel(_12));  // open: en
  Multiplexer #(.width(32)) multiplexer_14 (
    .in0(t4), .in1(Write_Data), .out(multiplexer_14_out), .sel(_13));  // open: en
  Multiplexer #(.width(32)) multiplexer_15 (
    .in0(t5), .in1(Write_Data), .out(multiplexer_15_out), .sel(_14));  // open: en
  Multiplexer #(.width(32)) multiplexer_16 (
    .in0(t6), .in1(Write_Data), .out(multiplexer_16_out), .sel(_15));  // open: en
  Multiplexer #(.width(32)) multiplexer_17 (
    .in0(t7), .in1(Write_Data), .out(multiplexer_17_out), .sel(_16));  // open: en
  Multiplexer #(.width(32)) multiplexer_18 (
    .in0(s0_Value), .in1(Write_Data), .out(multiplexer_18_out), .sel(_17));  // open: en
  Multiplexer #(.width(32)) multiplexer_19 (
    .in0(s1_Value), .in1(Write_Data), .out(multiplexer_19_out), .sel(_18));  // open: en
  Multiplexer #(.width(32)) multiplexer_20 (
    .in0(s2_Value), .in1(Write_Data), .out(multiplexer_20_out), .sel(_19));  // open: en
  Multiplexer #(.width(32)) multiplexer_21 (
    .in0(s3), .in1(Write_Data), .out(multiplexer_21_out), .sel(_20));  // open: en
  Multiplexer #(.width(32)) multiplexer_22 (
    .in0(s4), .in1(Write_Data), .out(multiplexer_22_out), .sel(_21));  // open: en
  Multiplexer #(.width(32)) multiplexer_23 (
    .in0(s5), .in1(Write_Data), .out(multiplexer_23_out), .sel(_22));  // open: en
  Register #(.width(32)) register_11 (.D(multiplexer_12_out), .Q(t2), .clk(Clock));  // open: en, clr
  Register #(.width(32)) register_12 (.D(multiplexer_13_out), .Q(t3), .clk(Clock));  // open: en, clr
  Register #(.width(32)) register_13 (.D(multiplexer_14_out), .Q(t4), .clk(Clock));  // open: en, clr
  Register #(.width(32)) register_14 (.D(multiplexer_15_out), .Q(t5), .clk(Clock));  // open: en, clr
  Register #(.width(32)) register_15 (.D(multiplexer_16_out), .Q(t6), .clk(Clock));  // open: en, clr
  Register #(.width(32)) register_16 (.D(multiplexer_17_out), .Q(t7), .clk(Clock));  // open: en, clr
  Register #(.width(32)) register_17 (.D(multiplexer_18_out), .Q(s0_Value), .clk(Clock));  // open: en, clr
  Register #(.width(32)) register_18 (.D(multiplexer_19_out), .Q(s1_Value), .clk(Clock));  // open: en, clr
  Register #(.width(32)) register_19 (.D(multiplexer_20_out), .Q(s2_Value), .clk(Clock));  // open: en, clr
  Register #(.width(32)) register_20 (.D(multiplexer_21_out), .Q(s3), .clk(Clock));  // open: en, clr
  Register #(.width(32)) register_21 (.D(multiplexer_22_out), .Q(s4), .clk(Clock));  // open: en, clr
  Register #(.width(32)) register_22 (.D(multiplexer_23_out), .Q(s5), .clk(Clock));  // open: en, clr
  Multiplexer #(.width(32)) multiplexer_24 (
    .in0(s6), .in1(Write_Data), .out(multiplexer_24_out), .sel(_23));  // open: en
  Multiplexer #(.width(32)) multiplexer_25 (
    .in0(s7), .in1(Write_Data), .out(multiplexer_25_out), .sel(_24));  // open: en
  Multiplexer #(.width(32)) multiplexer_26 (
    .in0(t8), .in1(Write_Data), .out(multiplexer_26_out), .sel(_25));  // open: en
  Multiplexer #(.width(32)) multiplexer_27 (
    .in0(t9), .in1(Write_Data), .out(multiplexer_27_out), .sel(_26));  // open: en
  Multiplexer #(.width(32)) multiplexer_28 (
    .in0(k0), .in1(Write_Data), .out(multiplexer_28_out), .sel(_27));  // open: en
  Multiplexer #(.width(32)) multiplexer_29 (
    .in0(k1), .in1(Write_Data), .out(multiplexer_29_out), .sel(_28));  // open: en
  Multiplexer #(.width(32)) multiplexer_30 (
    .in0(gp), .in1(Write_Data), .out(multiplexer_30_out), .sel(_29));  // open: en
  Multiplexer #(.width(32)) multiplexer_31 (
    .in0(sp_Value), .in1(Write_Data), .out(multiplexer_31_out), .sel(_30));  // open: en
  Multiplexer #(.width(32)) multiplexer_32 (
    .in0(fp), .in1(Write_Data), .out(multiplexer_32_out), .sel(_31));  // open: en
  Multiplexer #(.width(32)) multiplexer_33 (
    .in0(ra_Value), .in1(Write_Data), .out(multiplexer_33_out), .sel(_32));  // open: en
  Register #(.width(32)) register_23 (.D(multiplexer_24_out), .Q(s6), .clk(Clock));  // open: en, clr
  Register #(.width(32)) register_24 (.D(multiplexer_25_out), .Q(s7), .clk(Clock));  // open: en, clr
  Register #(.width(32)) register_25 (.D(multiplexer_26_out), .Q(t8), .clk(Clock));  // open: en, clr
  Register #(.width(32)) register_26 (.D(multiplexer_27_out), .Q(t9), .clk(Clock));  // open: en, clr
  Register #(.width(32)) register_27 (.D(multiplexer_28_out), .Q(k0), .clk(Clock));  // open: en, clr
  Register #(.width(32)) register_28 (.D(multiplexer_29_out), .Q(k1), .clk(Clock));  // open: en, clr
  Register #(.width(32)) register_29 (.D(multiplexer_30_out), .Q(gp), .clk(Clock));  // open: en, clr
  Register #(.width(32)) register_30 (.D(multiplexer_31_out), .Q(sp_Value), .clk(Clock));  // open: en, clr
  Register #(.width(32)) register_31 (.D(multiplexer_32_out), .Q(fp), .clk(Clock));  // open: en, clr
  Register #(.width(32)) register_32 (.D(multiplexer_33_out), .Q(ra_Value), .clk(Clock));  // open: en, clr
  Demultiplexer #(.select(5)) demultiplexer_1 (
    .out0(_1), .out1(_2), .out2(_3), .out3(_4), .out4(_5), .out5(_6), .out6(_7), .out7(_8), .out8(_9),
    .out9(_10), .out10(_11), .out11(_12), .out12(_13), .out13(_14), .out14(_15), .out15(_16), .out16(_17),
    .out17(_18), .out18(_19), .out19(_20), .out20(_21), .out21(_22), .out22(_23), .out23(_24), .out24(_25),
    .out25(_26), .out26(_27), .out27(_28), .out28(_29), .out29(_30), .out30(_31), .out31(_32),
    .in(Write_Enable), .sel(Write_Register));  // open: en
  Multiplexer #(.select(5), .width(32)) multiplexer_34 (
    .in0(zero), .in1(at), .in2(v0), .in3(v1), .in4(a0), .in5(a1), .in6(a2), .in7(a3), .in8(t0), .in9(t1),
    .in10(t2), .in11(t3), .in12(t4), .in13(t5), .in14(t6), .in15(t7), .in16(s0_Value), .in17(s1_Value),
    .in18(s2_Value), .in19(s3), .in20(s4), .in21(s5), .in22(s6), .in23(s7), .in24(t8), .in25(t8), .in26(k0),
    .in27(k1), .in28(gp), .in29(sp_Value), .in30(fp), .in31(ra_Value), .out(Read_Data_2),
    .sel(Read_Register_2));  // open: en

  // Other names for the same wires on the sheet: clk = Clock; ra[31:0] = ra_Value; read_data1[31:0] = Read_Data_1;
  //   read_data2[31:0] = Read_Data_2; read_reg1[4:0] = Read_Register_1; read_reg2[4:0] = Read_Register_2;
  //   S0[31:0] = s0_Value; S1[31:0] = s1_Value; S2[31:0] = s2_Value; sp[31:0] = sp_Value; write_en = Write_Enable;
  //   write_reg[4:0] = Write_Register

  // Notes on the sheet:
  //   INPUTS to your circuit
  //   DON'T CHANGE THE LOCATIONS OF THE INPUTS AND OUTPUTS!
  //   16
  //   Get Specific data from a the register specified by read_reg1
  //   17
  //   These are DEBUG/TEST outputs from your circuit.
  //   18
  //   31
  //   read data 1
  //   29
  //   OUTPUTS from your circuit
  //   Determine if you are able to write to a specific register
  //   Get Information from a specific register determined by read-reg2
endmodule

module ALUOp (
  input  [5:0] funct,
  input  [5:0] Opcode,
  output [3:0] ALUOp
);

  wire and_11_out, not_1_out, not_2_out, not_3_out, not_4_out, not_5_out, not_6_out, not_7_out, not_8_out,
       not_9_out, not_10_out, not_11_out, not_12_out, not_13_out, not_14_out, not_15_out, not_16_out,
       not_17_out, not_18_out, not_19_out, not_20_out, not_21_out, not_22_out, not_23_out, not_24_out,
       not_25_out, not_26_out, not_27_out, not_28_out, not_29_out, not_30_out, not_31_out, not_32_out,
       not_33_out, not_34_out, not_35_out, not_36_out, not_37_out, not_38_out, not_39_out, not_40_out,
       not_41_out, not_42_out, not_43_out, not_44_out, not_45_out, not_46_out, not_47_out, not_48_out,
       not_49_out, not_50_out, not_51_out, not_52_out, not_53_out, not_54_out, not_55_out, not_56_out,
       not_57_out, not_58_out, not_59_out, not_60_out, not_61_out, not_62_out, not_63_out, not_64_out,
       not_65_out, not_66_out, not_67_out, not_68_out, not_69_out, not_70_out, not_71_out, not_72_out,
       not_73_out, not_74_out, not_75_out;
  wire [0:0] and_1_out, and_2_out, and_3_out, and_4_out, and_5_out, and_6_out, and_7_out, and_8_out,
       and_9_out, and_10_out, and_12_out, and_13_out, and_14_out, and_15_out, and_16_out, and_17_out,
       and_18_out, and_19_out;
  wire [3:0] adder_1_out, adder_2_out, adder_3_out, adder_4_out, adder_5_out, adder_6_out, adder_7_out,
       adder_8_out, adder_9_out, adder_10_out, adder_11_out, adder_12_out, adder_13_out, adder_14_out,
       adder_15_out, adder_16_out, multiplier_1_out, multiplier_2_out, multiplier_3_out, multiplier_4_out,
       multiplier_5_out, multiplier_6_out, multiplier_7_out, multiplier_8_out, multiplier_9_out,
       multiplier_10_out, multiplier_11_out, multiplier_12_out, multiplier_13_out, multiplier_14_out,
       multiplier_15_out, multiplier_16_out, multiplier_17_out, multiplier_18_out;

  not not_1 (not_1_out, funct[0]);
  not not_2 (not_2_out, funct[1]);
  not not_3 (not_3_out, funct[2]);
  not not_4 (not_4_out, funct[3]);
  not not_5 (not_5_out, funct[4]);
  not not_6 (not_6_out, funct[5]);
  not not_7 (not_7_out, funct[0]);
  not not_8 (not_8_out, funct[2]);
  not not_9 (not_9_out, funct[3]);
  not not_10 (not_10_out, funct[4]);
  not not_11 (not_11_out, funct[5]);
  not not_12 (not_12_out, funct[2]);
  not not_13 (not_13_out, funct[3]);
  not not_14 (not_14_out, funct[4]);
  not not_15 (not_15_out, funct[5]);
  not not_16 (not_16_out, funct[0]);
  not not_17 (not_17_out, funct[1]);
  not not_18 (not_18_out, funct[2]);
  not not_19 (not_19_out, funct[3]);
  not not_20 (not_20_out, funct[4]);
  not not_21 (not_21_out, funct[1]);
  not not_22 (not_22_out, funct[2]);
  not not_23 (not_23_out, funct[3]);
  not not_24 (not_24_out, funct[4]);
  not not_25 (not_25_out, funct[0]);
  not not_26 (not_26_out, funct[1]);
  not not_27 (not_27_out, funct[3]);
  not not_28 (not_28_out, funct[4]);
  not not_29 (not_29_out, funct[1]);
  not not_30 (not_30_out, funct[3]);
  not not_31 (not_31_out, funct[4]);
  not not_32 (not_32_out, funct[0]);
  not not_33 (not_33_out, funct[3]);
  not not_34 (not_34_out, funct[4]);
  not not_35 (not_35_out, funct[0]);
  not not_36 (not_36_out, funct[2]);
  not not_37 (not_37_out, funct[4]);
  not not_38 (not_38_out, funct[2]);
  not not_39 (not_39_out, funct[4]);
  not not_40 (not_40_out, Opcode[0]);
  not not_41 (not_41_out, Opcode[1]);
  not not_42 (not_42_out, Opcode[2]);
  not not_43 (not_43_out, Opcode[3]);
  not not_44 (not_44_out, Opcode[4]);
  not not_45 (not_45_out, Opcode[5]);
  not not_46 (not_46_out, Opcode[1]);
  not not_47 (not_47_out, Opcode[2]);
  not not_48 (not_48_out, Opcode[4]);
  not not_49 (not_49_out, Opcode[5]);
  not not_50 (not_50_out, Opcode[0]);
  not not_51 (not_51_out, Opcode[1]);
  not not_52 (not_52_out, Opcode[2]);
  not not_53 (not_53_out, Opcode[4]);
  not not_54 (not_54_out, Opcode[5]);
  not not_55 (not_55_out, Opcode[2]);
  not not_56 (not_56_out, Opcode[3]);
  not not_57 (not_57_out, Opcode[4]);
  not not_58 (not_58_out, Opcode[5]);
  not not_59 (not_59_out, Opcode[0]);
  not not_60 (not_60_out, Opcode[1]);
  not not_61 (not_61_out, Opcode[4]);
  not not_62 (not_62_out, Opcode[5]);
  not not_63 (not_63_out, Opcode[1]);
  not not_64 (not_64_out, Opcode[4]);
  not not_65 (not_65_out, Opcode[5]);
  not not_66 (not_66_out, Opcode[0]);
  not not_67 (not_67_out, Opcode[3]);
  not not_68 (not_68_out, Opcode[4]);
  not not_69 (not_69_out, Opcode[0]);
  not not_70 (not_70_out, Opcode[2]);
  not not_71 (not_71_out, Opcode[4]);
  not not_72 (not_72_out, Opcode[5]);
  not not_73 (not_73_out, Opcode[2]);
  not not_74 (not_74_out, Opcode[4]);
  not not_75 (not_75_out, Opcode[5]);
  and and_1 (and_1_out[0], not_1_out, not_2_out, not_3_out, not_4_out, not_5_out, not_6_out);
  and and_2 (and_2_out[0], not_7_out, funct[1], not_8_out, not_9_out, not_10_out, not_11_out);
  and and_3 (and_3_out[0], funct[0], funct[1], not_12_out, not_13_out, not_14_out, not_15_out);
  and and_4 (and_4_out[0], not_16_out, not_17_out, not_18_out, not_19_out, not_20_out, funct[5]);
  and and_5 (and_5_out[0], funct[0], not_21_out, not_22_out, not_23_out, not_24_out, funct[5]);
  and and_6 (and_6_out[0], not_25_out, not_26_out, funct[2], not_27_out, not_28_out, funct[5]);
  and and_7 (and_7_out[0], funct[0], not_29_out, funct[2], not_30_out, not_31_out, funct[5]);
  and and_8 (and_8_out[0], not_32_out, funct[1], funct[2], not_33_out, not_34_out, funct[5]);
  and and_9 (and_9_out[0], not_35_out, funct[1], not_36_out, funct[3], not_37_out, funct[5]);
  and and_10 (and_10_out[0], funct[0], funct[1], not_38_out, funct[3], not_39_out, funct[5]);
  and and_11 (and_11_out, not_40_out, not_41_out, not_42_out, not_43_out, not_44_out, not_45_out);
  and and_12 (and_12_out[0], Opcode[0], not_46_out, not_47_out, Opcode[3], not_48_out, not_49_out);
  and and_13 (and_13_out[0], not_50_out, not_51_out, not_52_out, Opcode[3], not_53_out, not_54_out);
  and and_14 (and_14_out[0], Opcode[0], Opcode[1], not_55_out, not_56_out, not_57_out, not_58_out);
  and and_15 (and_15_out[0], not_59_out, not_60_out, Opcode[2], Opcode[3], not_61_out, not_62_out);
  and and_16 (and_16_out[0], Opcode[0], not_63_out, Opcode[2], Opcode[3], not_64_out, not_65_out);
  and and_17 (and_17_out[0], not_66_out, Opcode[1], Opcode[2], not_67_out, not_68_out, Opcode[5]);
  and and_18 (and_18_out[0], not_69_out, Opcode[1], not_70_out, Opcode[3], not_71_out, not_72_out);
  and and_19 (and_19_out[0], Opcode[0], Opcode[1], not_73_out, Opcode[3], not_74_out, not_75_out);
  Multiplier #(.width(4)) multiplier_1 (
    .a({3'b000, and_1_out[0]}), .b(4'b0000), .out(multiplier_1_out));  // open: cin, cout
  Multiplier #(.width(4)) multiplier_2 (
    .a({3'b000, and_2_out[0]}), .b(4'b0001), .out(multiplier_2_out));  // open: cin, cout
  Multiplier #(.width(4)) multiplier_3 (
    .a({3'b000, and_3_out[0]}), .b(4'b0010), .out(multiplier_3_out));  // open: cin, cout
  Multiplier #(.width(4)) multiplier_4 (
    .a({3'b000, and_4_out[0]}), .b(4'b0011), .out(multiplier_4_out));  // open: cin, cout
  Multiplier #(.width(4)) multiplier_5 (
    .a({3'b000, and_5_out[0]}), .b(4'b0100), .out(multiplier_5_out));  // open: cin, cout
  Multiplier #(.width(4)) multiplier_6 (
    .a({3'b000, and_6_out[0]}), .b(4'b0111), .out(multiplier_6_out));  // open: cin, cout
  Multiplier #(.width(4)) multiplier_7 (
    .a({3'b000, and_7_out[0]}), .b(4'b1000), .out(multiplier_7_out));  // open: cin, cout
  Multiplier #(.width(4)) multiplier_8 (
    .a({3'b000, and_8_out[0]}), .b(4'b1001), .out(multiplier_8_out));  // open: cin, cout
  Multiplier #(.width(4)) multiplier_9 (
    .a({3'b000, and_9_out[0]}), .b(4'b1010), .out(multiplier_9_out));  // open: cin, cout
  Multiplier #(.width(4)) multiplier_10 (
    .a({3'b000, and_10_out[0]}), .b(4'b1011), .out(multiplier_10_out));  // open: cin, cout
  Multiplier #(.width(4)) multiplier_11 (
    .a({3'b000, and_12_out[0]}), .b(4'b0100), .out(multiplier_11_out));  // open: cin, cout
  Multiplier #(.width(4)) multiplier_12 (
    .a({3'b000, and_13_out[0]}), .b(4'b0011), .out(multiplier_12_out));  // open: cin, cout
  Multiplier #(.width(4)) multiplier_13 (
    .a({3'b000, and_14_out[0]}), .b(4'b0011), .out(multiplier_13_out));  // open: cin, cout
  Multiplier #(.width(4)) multiplier_14 (
    .a({3'b000, and_15_out[0]}), .b(4'b0111), .out(multiplier_14_out));  // open: cin, cout
  Multiplier #(.width(4)) multiplier_15 (
    .a({3'b000, and_16_out[0]}), .b(4'b1000), .out(multiplier_15_out));  // open: cin, cout
  Multiplier #(.width(4)) multiplier_16 (
    .a({3'b000, and_17_out[0]}), .b(4'b1001), .out(multiplier_16_out));  // open: cin, cout
  Multiplier #(.width(4)) multiplier_17 (
    .a({3'b000, and_18_out[0]}), .b(4'b1010), .out(multiplier_17_out));  // open: cin, cout
  Multiplier #(.width(4)) multiplier_18 (
    .a({3'b000, and_19_out[0]}), .b(4'b1011), .out(multiplier_18_out));  // open: cin, cout
  Adder #(.width(4)) adder_1 (.a(multiplier_1_out), .b(multiplier_2_out), .out(adder_1_out));  // open: cin, cout
  Adder #(.width(4)) adder_2 (.a(multiplier_3_out), .b(multiplier_4_out), .out(adder_2_out));  // open: cin, cout
  Adder #(.width(4)) adder_3 (.a(multiplier_5_out), .b(multiplier_6_out), .out(adder_3_out));  // open: cin, cout
  Adder #(.width(4)) adder_4 (.a(multiplier_7_out), .b(multiplier_8_out), .out(adder_4_out));  // open: cin, cout
  Adder #(.width(4)) adder_5 (.a(multiplier_9_out), .b(multiplier_10_out), .out(adder_5_out));  // open: cin, cout
  Adder #(.width(4)) adder_6 (.a(multiplier_11_out), .b(multiplier_12_out), .out(adder_6_out));  // open: cin, cout
  Adder #(.width(4)) adder_7 (.a(multiplier_13_out), .b(multiplier_14_out), .out(adder_7_out));  // open: cin, cout
  Adder #(.width(4)) adder_8 (.a(multiplier_15_out), .b(multiplier_16_out), .out(adder_8_out));  // open: cin, cout
  Adder #(.width(4)) adder_9 (.a(multiplier_17_out), .b(multiplier_18_out), .out(adder_9_out));  // open: cin, cout
  Adder #(.width(4)) adder_10 (.a(adder_1_out), .b(adder_2_out), .out(adder_10_out));  // open: cin, cout
  Adder #(.width(4)) adder_11 (.a(adder_3_out), .b(adder_4_out), .out(adder_11_out));  // open: cin, cout
  Adder #(.width(4)) adder_12 (.a(adder_8_out), .b(adder_9_out), .out(adder_12_out));  // open: cin, cout
  Adder #(.width(4)) adder_13 (.a(adder_10_out), .b(adder_11_out), .out(adder_13_out));  // open: cin, cout
  Adder #(.width(4)) adder_14 (.a(adder_7_out), .b(adder_12_out), .out(adder_14_out));  // open: cin, cout
  Adder #(.width(4)) adder_15 (.a(adder_13_out), .b(adder_5_out), .out(adder_15_out));  // open: cin, cout
  Adder #(.width(4)) adder_16 (.a(adder_6_out), .b(adder_14_out), .out(adder_16_out));  // open: cin, cout
  Multiplexer #(.width(4)) multiplexer_1 (
    .in0(adder_16_out), .in1(adder_15_out), .out(ALUOp), .sel(and_11_out));  // open: en

  // Notes on the sheet:
  //   sll
  //   srl
  //   sra
  //   add
  //   addu
  //   and
  //   or
  //   xor
  //   slt
  //   sltu
  //   addiu
  //   addi
  //   jal
  //   andi
  //   ori
  //   xor
  //   slti
  //   sltiu
endmodule
