// Logisim project control.circ as structural Verilog: 8 circuits, main circuit Control
module Control (
  input  [5:0] in_1,
  output RegDst,
  output Jump,
  output Branch,
  output MemRead,
  output MemtoReg,
  output MemWrite,
  output ALUSrc,
  output RegWrite
);

  RegDst regdst_1 (.Opcode(in_1), .RegDst(RegDst));
  Jump jump_1 (.Opcode(in_1), .Jump(Jump));
  Branch branch_1 (.Opcode(in_1), .Branch(Branch));
  MemRead_MemtoReg memread_memtoreg_1 (.Opcode(in_1), .MemRead_MemtoReg(MemRead));
  MemRead_MemtoReg memread_memtoreg_2 (.Opcode(in_1), .MemRead_MemtoReg(MemtoReg));
  MemWrite memwrite_1 (.Opcode(in_1), .MemWrite(MemWrite));
  ALUSrc alusrc_1 (.Opcode(in_1), .ALUSrc(ALUSrc));
  RegWrite regwrite_1 (.Opcode(in_1), .RegWrite(RegWrite));

  // Other names for the same wires on the sheet: Opcode[5:0] = in_1
endmodule

module RegDst (
  input  [5:0] Opcode,
  output RegDst
);

  wire not_1_out, not_2_out, not_3_out, not_4_out, not_5_out, not_6_out;

  not not_1 (not_1_out, Opcode[0]);
  not not_2 (not_2_out, Opcode[1]);
  not not_3 (not_3_out, Opcode[2]);
  not not_4 (not_4_out, Opcode[3]);
  not not_5 (not_5_out, Opcode[4]);
  not not_6 (not_6_out, Opcode[5]);
  and and_1 (RegDst, not_1_out, not_2_out, not_3_out, not_4_out, not_5_out, not_6_out);

  // Notes on the sheet:
  //   R-Type
endmodule

module Jump (
  input  [5:0] Opcode,
  output Jump
);

  wire and_1_out, and_2_out, not_1_out, not_2_out, not_3_out, not_4_out, not_5_out, not_6_out, not_7_out,
       not_8_out, not_9_out;

  not not_1 (not_1_out, Opcode[0]);
  not not_2 (not_2_out, Opcode[2]);
  not not_3 (not_3_out, Opcode[3]);
  not not_4 (not_4_out, Opcode[4]);
  not not_5 (not_5_out, Opcode[5]);
  not not_6 (not_6_out, Opcode[2]);
  not not_7 (not_7_out, Opcode[3]);
  not not_8 (not_8_out, Opcode[4]);
  not not_9 (not_9_out, Opcode[5]);
  and and_1 (and_1_out, not_1_out, Opcode[1], not_2_out, not_3_out, not_4_out, not_5_out);
  and and_2 (and_2_out, Opcode[0], Opcode[1], not_6_out, not_7_out, not_8_out, not_9_out);
  or or_1 (Jump, and_1_out, and_2_out);

  // Notes on the sheet:
  //   j instruction
  //   jal instruction
endmodule

module Branch (
  input  [5:0] Opcode,
  output Branch
);

  wire and_1_out, and_2_out, and_3_out, not_1_out, not_2_out, not_3_out, not_4_out, not_5_out, not_6_out,
       not_7_out, not_8_out, not_9_out, not_10_out, not_11_out, not_12_out, not_13_out, not_14_out;

  not not_1 (not_1_out, Opcode[0]);
  not not_2 (not_2_out, Opcode[1]);
  not not_3 (not_3_out, Opcode[3]);
  not not_4 (not_4_out, Opcode[4]);
  not not_5 (not_5_out, Opcode[5]);
  not not_6 (not_6_out, Opcode[1]);
  not not_7 (not_7_out, Opcode[3]);
  not not_8 (not_8_out, Opcode[4]);
  not not_9 (not_9_out, Opcode[5]);
  not not_10 (not_10_out, Opcode[1]);
  not not_11 (not_11_out, Opcode[2]);
  not not_12 (not_12_out, Opcode[3]);
  not not_13 (not_13_out, Opcode[4]);
  not not_14 (not_14_out, Opcode[5]);
  and and_1 (and_1_out, not_1_out, not_2_out, Opcode[2], not_3_out, not_4_out, not_5_out);
  and and_2 (and_2_out, Opcode[0], not_6_out, Opcode[2], not_7_out, not_8_out, not_9_out);
  and and_3 (and_3_out, Opcode[0], not_10_out, not_11_out, not_12_out, not_13_out, not_14_out);
  or or_1 (Branch, and_1_out, and_2_out, and_3_out);

  // Notes on the sheet:
  //   beq
  //   bne
  //   bgezal
endmodule

module MemRead_MemtoReg (
  input  [5:0] Opcode,
  output MemRead_MemtoReg
);

  wire not_1_out, not_2_out, not_3_out;

  not not_1 (not_1_out, Opcode[2]);
  not not_2 (not_2_out, Opcode[3]);
  not not_3 (not_3_out, Opcode[4]);
  and and_1 (MemRead_MemtoReg, Opcode[0], Opcode[1], not_1_out, not_2_out, not_3_out, Opcode[5]);
endmodule

module MemWrite (
  input  [5:0] Opcode,
  output MemWrite
);

  wire not_1_out, not_2_out;

  not not_1 (not_1_out, Opcode[2]);
  not not_2 (not_2_out, Opcode[4]);
  and and_1 (MemWrite, Opcode[0], Opcode[1], not_1_out, Opcode[3], not_2_out, Opcode[5]);

  // Notes on the sheet:
  //   R-Type
endmodule

module RegWrite (
  input  [5:0] Opcode,
  output RegWrite
);

  wire and_1_out, and_2_out, and_3_out, and_4_out, and_5_out, and_6_out, and_7_out, and_8_out, and_9_out,
       and_10_out, not_1_out, not_2_out, not_3_out, not_4_out, not_5_out, not_6_out, not_7_out, not_8_out,
       not_9_out, not_10_out, not_11_out, not_12_out, not_13_out, not_14_out, not_15_out, not_16_out,
       not_17_out, not_18_out, not_19_out, not_20_out, not_21_out, not_22_out, not_23_out, not_24_out,
       not_25_out, not_26_out, not_27_out, not_28_out, not_29_out, not_30_out, not_31_out, not_32_out,
       not_33_out, not_34_out, not_35_out, not_36_out, not_37_out, not_38_out, not_39_out, not_40_out,
       not_41_out;

  not not_1 (not_1_out, Opcode[0]);
  not not_2 (not_2_out, Opcode[1]);
  not not_3 (not_3_out, Opcode[2]);
  not not_4 (not_4_out, Opcode[3]);
  not not_5 (not_5_out, Opcode[4]);
  not not_6 (not_6_out, Opcode[5]);
  not not_7 (not_7_out, Opcode[2]);
  not not_8 (not_8_out, Opcode[3]);
  not not_9 (not_9_out, Opcode[4]);
  not not_10 (not_10_out, Opcode[1]);
  not not_11 (not_11_out, Opcode[2]);
  not not_12 (not_12_out, Opcode[4]);
  not not_13 (not_13_out, Opcode[5]);
  not not_14 (not_14_out, Opcode[0]);
  not not_15 (not_15_out, Opcode[1]);
  not not_16 (not_16_out, Opcode[2]);
  not not_17 (not_17_out, Opcode[4]);
  not not_18 (not_18_out, Opcode[5]);
  not not_19 (not_19_out, Opcode[0]);
  not not_20 (not_20_out, Opcode[1]);
  not not_21 (not_21_out, Opcode[4]);
  not not_22 (not_22_out, Opcode[5]);
  not not_23 (not_23_out, Opcode[1]);
  not not_24 (not_24_out, Opcode[4]);
  not not_25 (not_25_out, Opcode[5]);
  not not_26 (not_26_out, Opcode[0]);
  not not_27 (not_27_out, Opcode[2]);
  not not_28 (not_28_out, Opcode[4]);
  not not_29 (not_29_out, Opcode[5]);
  not not_30 (not_30_out, Opcode[2]);
  not not_31 (not_31_out, Opcode[4]);
  not not_32 (not_32_out, Opcode[5]);
  not not_33 (not_33_out, Opcode[2]);
  not not_34 (not_34_out, Opcode[3]);
  not not_35 (not_35_out, Opcode[4]);
  not not_36 (not_36_out, Opcode[5]);
  not not_37 (not_37_out, Opcode[1]);
  not not_38 (not_38_out, Opcode[2]);
  not not_39 (not_39_out, Opcode[3]);
  not not_40 (not_40_out, Opcode[4]);
  not not_41 (not_41_out, Opcode[5]);
  and and_1 (and_1_out, not_1_out, not_2_out, not_3_out, not_4_out, not_5_out, not_6_out);
  and and_2 (and_2_out, Opcode[0], Opcode[1], not_7_out, not_8_out, not_9_out, Opcode[5]);
  and and_3 (and_3_out, Opcode[0], not_10_out, not_11_out, Opcode[3], not_12_out, not_13_out);
  and and_4 (and_4_out, not_14_out, not_15_out, not_16_out, Opcode[3], not_17_out, not_18_out);
  and and_5 (and_5_out, not_19_out, not_20_out, Opcode[2], Opcode[3], not_21_out, not_22_out);
  and and_6 (and_6_out, Opcode[0], not_23_out, Opcode[2], Opcode[3], not_24_out, not_25_out);
  and and_7 (and_7_out, not_26_out, Opcode[1], not_27_out, Opcode[3], not_28_out, not_29_out);
  and and_8 (and_8_out, Opcode[0], Opcode[1], not_30_out, Opcode[3], not_31_out, not_32_out);
  and and_9 (and_9_out, Opcode[0], Opcode[1], not_33_out, not_34_out, not_35_out, not_36_out);
  and and_10 (and_10_out, Opcode[0], not_37_out, not_38_out, not_39_out, not_40_out, not_41_out);
  or or_1 (RegWrite, and_1_out, and_2_out, and_3_out, and_5_out, and_6_out, and_7_out, and_8_out, and_4_out, and_9_out, and_10_out);

  // Notes on the sheet:
  //   R-Type
  //   Load Word
  //   Load Word
  //   jal
  //   jal
endmodule

module ALUSrc (
  input  [5:0] Opcode,
  output ALUSrc
);

  wire and_1_out, and_2_out, and_3_out, and_4_out, and_5_out, and_6_out, and_7_out, and_8_out, and_9_out,
       not_1_out, not_2_out, not_3_out, not_4_out, not_5_out, not_6_out, not_7_out, not_8_out, not_9_out,
       not_10_out, not_11_out, not_12_out, not_13_out, not_14_out, not_15_out, not_16_out, not_17_out,
       not_18_out, not_19_out, not_20_out, not_21_out, not_22_out, not_23_out, not_24_out, not_25_out,
       not_26_out, not_27_out, not_28_out, not_29_out, not_30_out, not_31_out, not_32_out, not_33_out,
       not_34_out;

  not not_1 (not_1_out, Opcode[1]);
  not not_2 (not_2_out, Opcode[2]);
  not not_3 (not_3_out, Opcode[4]);
  not not_4 (not_4_out, Opcode[5]);
  not not_5 (not_5_out, Opcode[0]);
  not not_6 (not_6_out, Opcode[1]);
  not not_7 (not_7_out, Opcode[2]);
  not not_8 (not_8_out, Opcode[4]);
  not not_9 (not_9_out, Opcode[5]);
  not not_10 (not_10_out, Opcode[0]);
  not not_11 (not_11_out, Opcode[2]);
  not not_12 (not_12_out, Opcode[4]);
  not not_13 (not_13_out, Opcode[5]);
  not not_14 (not_14_out, Opcode[2]);
  not not_15 (not_15_out, Opcode[4]);
  not not_16 (not_16_out, Opcode[5]);
  not not_17 (not_17_out, Opcode[2]);
  not not_18 (not_18_out, Opcode[3]);
  not not_19 (not_19_out, Opcode[4]);
  not not_20 (not_20_out, Opcode[5]);
  not not_21 (not_21_out, Opcode[1]);
  not not_22 (not_22_out, Opcode[2]);
  not not_23 (not_23_out, Opcode[3]);
  not not_24 (not_24_out, Opcode[4]);
  not not_25 (not_25_out, Opcode[5]);
  and and_1 (and_1_out, Opcode[0], not_1_out, not_2_out, Opcode[3], not_3_out, not_4_out);
  and and_2 (and_2_out, not_5_out, not_6_out, not_7_out, Opcode[3], not_8_out, not_9_out);
  and and_3 (and_3_out, not_10_out, Opcode[1], not_11_out, Opcode[3], not_12_out, not_13_out);
  and and_4 (and_4_out, Opcode[0], Opcode[1], not_14_out, Opcode[3], not_15_out, not_16_out);
  and and_5 (and_5_out, Opcode[0], Opcode[1], not_17_out, not_18_out, not_19_out, not_20_out);
  and and_6 (and_6_out, Opcode[0], not_21_out, not_22_out, not_23_out, not_24_out, not_25_out);
  not not_26 (not_26_out, Opcode[0]);
  not not_27 (not_27_out, Opcode[1]);
  not not_28 (not_28_out, Opcode[4]);
  not not_29 (not_29_out, Opcode[5]);
  not not_30 (not_30_out, Opcode[1]);
  not not_31 (not_31_out, Opcode[4]);
  not not_32 (not_32_out, Opcode[5]);
  not not_33 (not_33_out, Opcode[4]);
  not not_34 (not_34_out, Opcode[5]);
  and and_7 (and_7_out, not_26_out, not_27_out, Opcode[2], Opcode[3], not_28_out, not_29_out);
  and and_8 (and_8_out, Opcode[0], not_30_out, Opcode[2], Opcode[3], not_31_out, not_32_out);
  and and_9 (and_9_out, Opcode[0], Opcode[1], Opcode[2], Opcode[3], not_33_out, not_34_out);
  or or_1 (ALUSrc, and_7_out, and_8_out, and_9_out, and_1_out, and_2_out, and_3_out, and_4_out, and_5_out, and_6_out);

  // Notes on the sheet:
  //   addiu
  //   addi
  //   slti
  //   sltiu
  //   jal
  //   jal
  //   andi
  //   ori
  //   lui
endmodule
